// Digital circuit bool_unit.dig as structural Verilog
module bool_unit (
  input  [3:0] A,
  input  [3:0] B,
  input  LogSel,
  output [3:0] Result
);

  wire [3:0] and_1_out, or_1_out;

  assign and_1_out = A & B;  // And and_1, 4 bits wide
  assign or_1_out = A | B;  // Or or_1, 4 bits wide
  Multiplexer #(.Bits(4)) multiplexer_1 (.sel(LogSel), .in_0(and_1_out), .in_1(or_1_out), .out(Result));
endmodule

/* Test case bool_self_test:
A B LogSel Result
1 1 0 0
1 0 1 0
*/
