// Digital circuit wrong_bool_LED4.dig as structural Verilog
module wrong_bool_LED4 (
  input  load,
  input  Clock,
  input  B,
  input  C,
  input  A,
  input  D,
  output Fa,
  output Fb,
  output Fc,
  output Fd,
  output Fe,
  output Fg,
  output Ff
);

  wire A_t, A_t_t, and_1_out, and_2_out, and_3_out, and_4_out, and_5_out, and_6_out, and_7_out, and_8_out,
       and_9_out, and_10_out, and_11_out, and_12_out, and_13_out, and_14_out, and_15_out, and_16_out,
       and_17_out, and_18_out, and_19_out, and_20_out, and_21_out, and_22_out, and_23_out, and_24_out,
       and_25_out, and_26_out, and_27_out, and_28_out, B_t, B_t_t, C_t, C_t_t, D_t, D_t_t, nand_1_out,
       not_5_out, not_6_out, not_7_out, xnor_1_out, xor_1_out;

  Register register_1 (.D(A), .C(Clock), .en(load), .Q(A_t));
  Register register_2 (.D(B), .C(Clock), .en(load), .Q(B_t));
  Register register_3 (.D(C), .C(Clock), .en(load), .Q(C_t));
  Register register_4 (.D(D), .C(Clock), .en(load), .Q(D_t));
  not not_1 (A_t_t, A_t);
  not not_2 (B_t_t, B_t);
  not not_3 (C_t_t, C_t);
  not not_4 (D_t_t, D_t);
  and and_1 (and_1_out, B_t, D_t, A_t_t);
  and and_2 (and_2_out, B_t_t, D_t_t);
  and and_3 (and_3_out, B_t, C_t);
  and and_4 (and_4_out, A_t_t, C_t);
  and and_5 (and_5_out, C_t_t, B_t_t, A_t);
  and and_6 (and_6_out, C_t, D_t, A_t_t);
  and and_7 (and_7_out, B_t_t, D_t_t);
  and and_8 (and_8_out, B_t_t, C_t_t);
  and and_9 (and_9_out, A_t_t, C_t_t, D_t_t);
  and and_10 (and_10_out, D_t, C_t_t, A_t);
  and and_11 (and_11_out, B_t_t, A_t);
  and and_12 (and_12_out, C_t_t, D_t);
  and and_13 (and_13_out, B_t, A_t_t);
  and and_14 (and_14_out, A_t_t, D_t);
  and and_15 (and_15_out, C_t_t, B_t_t);
  or or_1 (Fc, and_11_out, and_12_out, and_13_out, and_14_out, and_15_out);
  or or_2 (Fa, and_1_out, and_2_out, and_3_out, and_4_out, and_5_out);
  or or_3 (Fb, and_6_out, and_7_out, and_8_out, and_9_out, and_10_out);
  Seven_Seg seven_seg_1 (.a(Fa), .b(Fb), .c(Fc), .d(Fd), .e(Fe), .f(Ff), .g(Fg), .dp(1'b0));
  xor xor_1 (xor_1_out, C_t, D_t);
  and and_16 (and_16_out, C_t_t, A_t);
  xnor xnor_1 (xnor_1_out, xor_1_out, B_t);
  not not_5 (not_5_out, A_t_t);
  not not_6 (not_6_out, B_t_t);
  not not_7 (not_7_out, C_t);
  and and_17 (and_17_out, C_t, A_t);
  and and_18 (and_18_out, B_t_t, D_t_t);
  and and_19 (and_19_out, D_t_t, C_t);
  and and_20 (and_20_out, B_t, A_t);
  and and_21 (and_21_out, C_t_t, D_t_t, A_t_t);
  and and_22 (and_22_out, A_t, B_t_t);
  and and_23 (and_23_out, A_t, C_t);
  and and_24 (and_24_out, B_t, C_t, D_t_t);
  and and_25 (and_25_out, B_t, C_t_t, A_t_t);
  and and_26 (and_26_out, B_t_t, C_t);
  and and_27 (and_27_out, D_t_t, B_t);
  and and_28 (and_28_out, B_t, C_t_t);
  nand nand_1 (nand_1_out, not_5_out, not_6_out, not_7_out);
  or or_4 (Fd, and_16_out, xnor_1_out, nand_1_out);
  or or_5 (Fe, and_17_out, and_18_out, and_19_out, and_20_out);
  or or_6 (Ff, and_21_out, and_22_out, and_23_out, and_24_out, and_25_out);
  or or_7 (Fg, A_t, and_26_out, and_27_out, and_28_out);

  // Other names for the same wires on the sheet: en = load
endmodule

/* Test case this_is_a_test:
A B C D load Clock Fa Fb Fc Fd Fe Ff Fg
# initial state: registers at 0, display shows '0'
0 0 0 0 0 C 1 1 1 1 1 1 0
# load 0101 (= 5): on next clock with load=1, registers capture
0 1 0 1 1 C 1 0 1 1 0 1 1
# hold: load=0, display stays at '5'
1 1 1 1 0 C 1 0 1 1 0 1 1
# load 1010 (= A): registers capture
1 0 1 0 1 C 1 1 1 0 1 1 1
# hold: load=0, X changes but display stays at 'A'
0 0 0 0 0 C 1 1 1 0 1 1 1
*/
