// Digital circuit demux_write_enable.dig as structural Verilog
module demux_write_enable (
  input  RegWrite,
  input  [4:0] WriteReg,
  output En0,
  output En31
);

  wire demultiplexer_1_out_0;

  Demultiplexer #(.Selector_Bits(5)) demultiplexer_1 (
    .sel(WriteReg), .in(RegWrite), .out_0(demultiplexer_1_out_0), .out_31(En31));  // open: out_1, out_2, out_3, out_4, out_5, out_6, out_7, out_8, out_9, out_10, out_11, out_12, out_13, out_14, out_15, out_16, out_17, out_18, out_19, out_20, out_21, out_22, out_23, out_24, out_25, out_26, out_27, out_28, out_29, out_30
  and and_1 (En0, demultiplexer_1_out_0, 1'b1);
endmodule
