// Digital circuit flipped_decoder_selfeed.dig as structural Verilog
module flipped_decoder_selfeed (
  input  [4:0] WriteReg,
  output En0
);

  Decoder #(.Selector_Bits(5)) decoder_1 (
    .sel(WriteReg), .out_0(En0));  // open: out_1, out_2, out_3, out_4, out_5, out_6, out_7, out_8, out_9, out_10, out_11, out_12, out_13, out_14, out_15, out_16, out_17, out_18, out_19, out_20, out_21, out_22, out_23, out_24, out_25, out_26, out_27, out_28, out_29, out_30, out_31

  // Other names for the same wires on the sheet: WR[4:0] = WriteReg
endmodule
