// Digital circuit regfile_write_read.dig as structural Verilog
module regfile_write_read (
  input  [7:0] WD,
  input  WE,
  input  [1:0] WA,
  input  clk,
  input  [1:0] RA,
  input  [1:0] RB,
  output [7:0] DA,
  output [7:0] DB
);

  RegisterFile #(.AddrBits(2), .Bits(8)) registerfile_1 (
    .Din(WD), .we(WE), .Rw(WA), .C(clk), .Ra(RA), .Rb(RB), .Da(DA), .Db(DB));
endmodule

/* Test case RegFile Test:
WD WE WA clk RA RB DA DB
5 1 0 C 0 1 5 0
7 1 1 C 0 1 5 7
9 0 2 C 2 1 0 7
3 1 1 C 1 0 3 5
*/
