// Digital circuit skew_parent.dig as structural Verilog
module skew_parent (
  input  P,
  input  Q,
  output Y
);

  // skew_child skew_child_1: pin names not known; wires that end beside it: P, Q, Y
endmodule
