// Digital circuit width_conflict.dig as structural Verilog
module width_conflict (
  input  [3:0] In,
  input  [3:0] B,
  output out_3
);

  and and_1 (out_3, B[0], B[0]);
  // Pins of 1 and 4 bits meet at B

  assign In = B;
endmodule
