// Digital circuit rom_lookup.dig as structural Verilog
module rom_lookup (
  input  [1:0] A,
  output [7:0] D
);

  ROM #(.Bits(8), .AddrBits(2)) rom_1 (.A(A), .sel(1'b1));  // open: D

  // Notes on the sheet:
  //   contents of rom_1 (hex, n*v repeats v):
  //   3,5,9,c
endmodule

/* Test case:
A D
0 3
1 5
2 9
3 12
*/
