// Digital circuit halfadder_mix.dig as structural Verilog
module halfadder_mix (
  input  A,
  input  B,
  output Sum,
  output Carry
);

  wire C1_d, N3_s, P1_inv_d;

  PFET P1_inv (.G(A), .S(1'b1), .D(P1_inv_d));
  NFET N1_inv (.G(A), .D(P1_inv_d), .S(1'b0));
  PFET P2_pass (.G(B), .S(A), .D(Sum));
  NFET N2_pass (.G(B), .D(Sum), .S(P1_inv_d));
  PFET C1 (.G(A), .S(1'b1), .D(C1_d));
  PFET C2 (.G(B), .S(1'b1), .D(C1_d));
  NFET N3 (.G(A), .D(C1_d), .S(N3_s));
  NFET N4 (.G(B), .D(N3_s), .S(1'b0));
  PFET P3_inv (.G(C1_d), .S(1'b1), .D(Carry));
  NFET N5_inv (.G(C1_d), .D(Carry), .S(1'b0));

  // Notes on the sheet:
  //   HALF ADDER from 10 transistors
  //   1) CMOS inverter -> Abar (2T)
  //   2) B selects A or Abar -> Sum (2T)
  //   3) CMOS NAND (4T)
  //   4) inverter -> Carry = A AND B (2T)
endmodule

/* Test case:
A B Sum Carry
0 0 0 0
0 1 1 0
1 0 1 0
1 1 0 1
*/
