// Digital circuit inverter_cmos.dig as structural Verilog
module inverter_cmos (
  input  A,
  output Y
);

  PFET P1_pmos (.G(A), .S(1'b1), .D(Y));
  NFET N1_nmos (.G(A), .D(Y), .S(1'b0));
endmodule

/* Test case:
A Y
0 1
1 0
*/
