// Digital circuit inverter_nmos.dig as structural Verilog
module inverter_nmos (
  input  A,
  output Y
);

  PullUp pullup_1 (.out(Y));
  NFET N1 (.G(A), .D(Y), .S(1'b0));

  // Notes on the sheet:
  //   NMOS inverter (1T + weak pull-up load)
endmodule

/* Test case:
A Y
0 1
1 0
*/
