// Digital circuit nand2_cmos.dig as structural Verilog
module nand2_cmos (
  input  A,
  input  B,
  output Y
);

  wire N1_s;

  PFET P1 (.G(A), .S(1'b1), .D(Y));
  NFET N1 (.G(A), .D(Y), .S(N1_s));
  NFET N2 (.G(B), .D(N1_s), .S(1'b0));
  PFET P2 (.G(B), .S(1'b1), .D(Y));
endmodule

/* Test case:
A B Y
0 0 1
0 1 1
1 0 1
1 1 0
*/
