// Digital circuit nand2_nmos.dig as structural Verilog
module nand2_nmos (
  input  A,
  input  B,
  output Y
);

  wire N1_s;

  PullUp pullup_1 (.out(Y));
  NFET N1 (.G(A), .D(Y), .S(N1_s));
  NFET N2 (.G(B), .D(N1_s), .S(1'b0));

  // Notes on the sheet:
  //   NMOS NAND (2T + weak pull-up load)
endmodule

/* Test case:
A B Y
0 0 1
0 1 1
1 0 1
1 1 0
*/
