// Digital circuit nand2_pmos.dig as structural Verilog
module nand2_pmos (
  input  A,
  input  B,
  output Y
);

  PFET PA (.G(A), .S(1'b1), .D(Y));
  PullDown pulldown_1 (.out(Y));
  PFET PB (.G(B), .S(1'b1), .D(Y));
endmodule

/* Test case:
A B Y
0 0 1
0 1 1
1 0 1
1 1 0
*/
