// Digital circuit nor2_cmos.dig as structural Verilog
module nor2_cmos (
  input  A,
  input  B,
  output Y
);

  wire P1_d;

  PFET P1 (.G(A), .S(1'b1), .D(P1_d));
  PFET P2 (.G(B), .S(P1_d), .D(Y));
  NFET N2 (.G(B), .D(Y), .S(1'b0));
  NFET N1 (.G(A), .D(Y), .S(1'b0));

  // Notes on the sheet:
  //   CMOS NOR (4T)
endmodule

/* Test case:
A B Y
0 0 1
0 1 0
1 0 0
1 1 0
*/
