// Digital circuit nor2_nmos.dig as structural Verilog
module nor2_nmos (
  input  A,
  input  B,
  output Y
);

  PullUp pullup_1 (.out(Y));
  NFET NA (.G(A), .D(Y), .S(1'b0));
  NFET NB (.G(B), .D(Y), .S(1'b0));
endmodule

/* Test case:
A B Y
0 0 1
0 1 0
1 0 0
1 1 0
*/
