// Digital circuit or2_cmos.dig as structural Verilog
module or2_cmos (
  input  A,
  input  B,
  output Y
);

  wire P1_d, P2_d;

  PFET P1 (.G(A), .S(1'b1), .D(P1_d));
  PFET P2 (.G(B), .S(P1_d), .D(P2_d));
  NFET N2 (.G(B), .D(P2_d), .S(1'b0));
  NFET N1 (.G(A), .D(P2_d), .S(1'b0));
  PFET P3 (.G(P2_d), .S(1'b1), .D(Y));
  NFET N3 (.G(P2_d), .D(Y), .S(1'b0));

  // Notes on the sheet:
  //   CMOS OR (6T) = NOR (4T) + inverter (2T)
endmodule

/* Test case:
A B Y
0 0 0
0 1 1
1 0 1
1 1 1
*/
