// Digital circuit xnor2_cmos.dig as structural Verilog
module xnor2_cmos (
  input  A,
  input  B,
  output Y
);

  wire P1_inv_d;

  PFET P1_inv (.G(A), .S(1'b1), .D(P1_inv_d));
  NFET N1_inv (.G(A), .D(P1_inv_d), .S(1'b0));
  PFET P2_pass (.G(B), .S(P1_inv_d), .D(Y));
  NFET N2_pass (.G(B), .D(Y), .S(A));

  // Notes on the sheet:
  //   CMOS XNOR (4T)
endmodule

/* Test case:
A B Y
0 0 1
0 1 0
1 0 0
1 1 1
*/
