// Digital circuit xor2_cmos.dig as structural Verilog
module xor2_cmos (
  input  A,
  input  B,
  output Y
);

  wire P1_inv_d;

  PFET P1_inv (.G(A), .S(1'b1), .D(P1_inv_d));
  NFET N1_inv (.G(A), .D(P1_inv_d), .S(1'b0));
  PFET P2_pass (.G(B), .S(A), .D(Y));
  NFET N2_pass (.G(B), .D(Y), .S(P1_inv_d));

  // Notes on the sheet:
  //   CMOS XOR (4T)
endmodule

/* Test case:
A B Y
0 0 0
0 1 1
1 0 1
1 1 0
*/
