// Digital circuit missing_top_subcircuit.dig as structural Verilog
module missing_top_subcircuit (
  input  A,
  output Y
);

  // ghost ghost_1: pin names not known; wires that end beside it: A, Y
endmodule
