// Digital circuit dlc_row_kknho6fo.dig as structural Verilog
module dlc_row_kknho6fo (
  input  [3:0] A,
  input  [3:0] B,
  input  [1:0] Op,
  input  Ci,
  output [3:0] Result,
  output Carry,
  output Zero,
  output Bit0
);

  wire add_1_c_o, add_2_c_o;
  wire [3:0] add_1_s, add_2_s, bool_unit_1_result, not_1_out;

  assign not_1_out = ~B;  // Not not_1, 4 bits wide
  Add #(.Bits(4)) add_1 (.a(A), .b(not_1_out), .c_i(Ci), .s(add_1_s), .c_o(add_1_c_o));
  Add #(.Bits(4)) add_2 (.a(A), .b(B), .c_i(Ci), .s(add_2_s), .c_o(add_2_c_o));
  bool_unit bool_unit_1 (.A(A), .B(B), .LogSel(Op[0]), .Result(bool_unit_1_result));
  Multiplexer multiplexer_1 (.sel(Op[0]), .in_0(add_2_c_o), .in_1(add_1_c_o), .out(Carry));
  Multiplexer #(.Selector_Bits(2), .Bits(4)) multiplexer_2 (
    .sel(Op), .in_0(add_2_s), .in_1(add_1_s), .in_2(bool_unit_1_result), .in_3(bool_unit_1_result),
    .out({Result[3:1], Bit0}));
  Comparator #(.Bits(4)) comparator_1 (.a({Result[3:1], Bit0}), .b(4'b0000), .eq(Zero));  // open: gt, lt

  assign Result[0] = Bit0;
endmodule

/* Test case:
A B Ci Op Result Carry Zero Bit0
5 3 0 0 8 0 0 0
*/
