// Digital circuit tier3_rom_machine.dig as structural Verilog
module tier3_rom_machine (
  input  clk,
  output [7:0] ACC,
  output [3:0] PCv
);

  wire [0:0] comparator_1_eq, comparator_1_lt;
  wire [1:0] op;
  wire [3:0] add_1_s;
  wire [7:0] add_2_s, imm, multiplexer_1_out;

  Register #(.Bits(4)) PC (.D(add_1_s), .C(clk), .en(1'b1), .Q(PCv));
  Add #(.Bits(4)) add_1 (.a(PCv), .b(4'b0001), .c_i(1'b0), .s(add_1_s));  // open: c_o
  ROM #(.AddrBits(4), .Bits(10)) Program (.A(PCv), .sel(1'b1), .D({op, imm}));
  Add #(.Bits(8)) add_2 (.a(ACC), .b(imm), .c_i(1'b0), .s(add_2_s));  // open: c_o
  Comparator #(.Bits(8)) comparator_1 (.a(ACC), .b(imm), .eq(comparator_1_eq[0]), .lt(comparator_1_lt[0]));  // open: gt
  Multiplexer #(.Selector_Bits(2), .Bits(8)) multiplexer_1 (
    .sel(op), .in_0(imm), .in_1(add_2_s), .in_2({{7{1'b0}}, comparator_1_lt[0]}),
    .in_3({{7{1'b0}}, comparator_1_eq[0]}), .out(multiplexer_1_out));
  Register #(.Bits(8)) u_ACC (.D(multiplexer_1_out), .C(clk), .en(1'b1), .Q(ACC));

  // Other names for the same wires on the sheet: pc[3:0] = PCv

  // Notes on the sheet:
  //   contents of Program (hex, n*v repeats v):
  //   25,117,240,17f,380,10f,20f,c3,3c4,133
endmodule

/* Test case rom machine:
clk ACC PCv
0 0 0
C 0x25 1
C 0x3C 2
C 1 3
C 0x80 4
C 1 5
C 0x10 6
C 0 7
C 0xC3 8
C 0 9
C 0x33 10
*/
